# Fritzing sketch 2020-02-03_Circuitry_final (saved by Fritzing 0.9.4)
stripboards: 1

parts:
  U1 = ESP32-38PinWide [part_number=ESP32-38PinWide]
  U2 = LIPO-2000mAh [package=lipo-2000]
  DC1 = DC_DC_XL4016 [package=board_screw]
  Part1 = KY-019 5V Relay Module [package="Breakout board"]
  M1 = RioRand LM2596
  Bauteil2 = InvenSense MPU6050
  HC-SR04_Sensor_1 = HC-SR04 Ultrasonic Distance Sensor
  HC-SR04_Sensor_2 = HC-SR04 Ultrasonic Distance Sensor
  ESP32_-_Back1 = ESP32 - CAM
  Bauteil7 = 12 NeoPixel Ring [part_number=1643]
  Bauteil1 = Adafruit PCA9685 PWM/Servo Breakout [part_number=815]
  Bauteil8 = FTDI Basic Programmer
  OLED1 = OLED 128x64 I2C Monochrome Display
  Mod1 = Voltage Sensor 25V
  BUTTON1 = Waterproof Pushbutton (white)
  J3 = male pin header, 14 pins [form="♂ (male)"]
  J4 = male pin header, 14 pins [form="♂ (male)"]
  J5 = female pin header, 2 pins [form="♀ (female)"]
  J6 = female pin header, 2 pins [form="♀ (female)"]
  J7 = female pin header, 2 pins [form="♀ (female)"]
  J8 = female pin header, 2 pins [form="♀ (female)"]
  J9 = female pin header, 2 pins [form="♀ (female)"]
  J10 = female pin header, 2 pins [form="♀ (female)"]
  J11 = female pin header, 2 pins [form="♀ (female)"]
  J12 = female pin header, 2 pins [form="♀ (female)"]
  J13 = female pin header, 2 pins [form="♀ (female)"]
  J14 = female pin header, 2 pins [form="♀ (female)"]
  J15 = female pin header, 2 pins [form="♀ (female)"]
  J16 = female pin header, 2 pins [form="♀ (female)"]
  J17 = female pin header, 2 pins [form="♀ (female)"]
  Bauteil10 = ACS712 Current Sensor 5A 20A 30A

nets:
  N1: U1.3.3, U1.GND, BUTTON1.no_name_yet#5, J17.pin1
  N2: U1.GPIO36, Mod1.S
  N3: U1.GPIO39, BUTTON1.no_name_yet#2, Bauteil10.2, Bauteil10.OUT
  N4: U1.GPIO34, HC-SR04_Sensor_2.ECHO
  N5: U1.GPIO35, HC-SR04_Sensor_1.ECHO
  N6: U1.GPIO32, HC-SR04_Sensor_1.TRIG
  N7: U1.GPIO33, HC-SR04_Sensor_2.TRIG
  N8: U1.GPIO25, Bauteil7.IN
  N9: U1.GPIO27, Part1.S
  N10: U1.VIN, J17.pin2
  N11: U1.GPIO2, BUTTON1.no_name_yet#4
  N12: U1.GPIO16, ESP32_-_Back1.GPIO13
  N13: U1.GPIO17, ESP32_-_Back1.GPIO16
  N14: U1.GPIO5, ESP32_-_Back1.GPIO12
  N15: U1.GPIO18, Bauteil1.SDA
  N16: U1.GPIO19, Bauteil1.SCL
  N17: U1.GPIO21, U1.GPIO1, U1.GPIO22
  N18: U2.+, BUTTON1.no_name_yet#1
  N19: U2.-, DC1.IN-
  N20: DC1.IN+, Mod1.VCC, Bauteil10.1
  N21: DC1.OUT+, Part1.Common, M1.Pin_1
  N22: DC1.OUT-, M1.Pin_2, Bauteil1.GND, J8.pin1
  N23: Part1.+, J7.pin2
  N24: Part1.-, J7.pin1
  N25: Part1.NO, Bauteil1.PWRIN
  N26: M1.Pin_3, M1.Pin_4
  N27: Bauteil2.VCC, J11.pin2
  N28: Bauteil2.GND, J11.pin1
  N29: Bauteil2.SCL, J12.pin2
  N30: Bauteil2.SDA, Bauteil2.XDA, J12.pin1
  N31: HC-SR04_Sensor_1.VCC, J14.pin2
  N32: HC-SR04_Sensor_1.GND, J14.pin1
  N33: HC-SR04_Sensor_2.VCC, J15.pin2
  N34: HC-SR04_Sensor_2.GND, J15.pin1
  N35: ESP32_-_Back1.GND#7, J16.pin1
  N36: ESP32_-_Back1.5V, J16.pin2
  N37: ESP32_-_Back1.3.3V, Bauteil8.POWER
  N38: ESP32_-_Back1.GPIO0, Bauteil8.DTR
  N39: ESP32_-_Back1.GPIO3_/_RX, Bauteil8.TXO
  N40: ESP32_-_Back1.GPIO1_/_TX, Bauteil8.RXI
  N41: ESP32_-_Back1.GND#16, Bauteil8.GND
  N42: Bauteil7.VDD, J13.pin2
  N43: Bauteil7.GND, J13.pin1
  N44: Bauteil1.VCC, J8.pin2
  N45: OLED1.GND, J5.pin1
  N46: OLED1.VDD, J5.pin2
  N47: OLED1.SCK, J6.pin1
  N48: OLED1.SDA, J6.pin2
  N49: Mod1.GND, Mod1.-, J9.pin1
  N50: Mod1.+, J9.pin2
  N51: J3.pin1, J3.pin8
  N52: J3.pin9, J3.pin10
  N53: J3.pin11, J3.pin14
  N54: J4.pin1, J4.pin8
  N55: J4.pin9, J4.pin10
  N56: J4.pin11, J4.pin14
  N57: J10.pin1, Bauteil10.GND
  N58: J10.pin2, Bauteil10.VCC

notes:
  :: XL4016 or SZBK07 ::
  7,4V - 8,4V IN to 6,5V OUT
  :: LM2596 ::
  6,5V IN to 5,0V OUT
  :: Pushbutton ::
  IN: 7,4V via C (common/feed)
  OUT: 7,4V via NO (normally open)
  Optional if Pushbutton with LED:
  Anode: GPIO2
  Cathode: GND
  :: PCA9685::
  CH0 - FLS CH3 - FRS CH6 - RLS CH9 - RRS
  CH1 - FLU CH4 - FRU CH7 - RLU CH10 - RRU
  CH2 - FLL CH5 - FRL CH8 - RLL CH11 - RRL
  :: ESP32-CAM Flashing ::
  Solder the pink Wire to the inner facing pad of the Reset Button (EN/CHIP_PU) and connect it to the RTS-Pin of the programmer (just solder an additional male pin header. To fit into the Counterpiece, remove the black plastik base of this single Pin.
  :: ESP32-CAM ::
  TX2/RX2 will be on GPIO16+13, when SD-Card is operated in 1Bit-Mode
  GPIO will be external RTC interrupt
  RX2/TX2 of main ESP32 will be at GPIO16 +17
  :: 12 RGB-LED Neopixel Ring ::
  Normal Operational Voltage is at 5V and thus above logic-level voltage! We would need something to lower the voltage.
  Here we connect to 3.3V directly as powersource, because in many cases it works as well, even though its out of spec!
  :: Current Sensor ::
  Make sure the current sensor measures towards -30A. This way it has its "nullposition" at 2.5V and it decreases output voltage by 66mV/A. This way we dont risk of damaging ADC input on ESP32, which can still only max to 3,3V (for protection set adc-channel to ADC_ATTEN_DB_11)
  :: Voltage Sensor ::
  Max Voltage at 8,4V / 5 = ~1,7V at ADC in. So set ADC-Channel attenuation to max. 2.2V for increased resolution instead of 3.3V. This equals ADC_ATTEN_DB_6)
  :: Power-Distribution Bus::
  -> double-sided prototyping PCB with 14x2 male pin-headers
  -> solder source from beneath (5V+GND, I2C-CLK+DAT, 3.3V+GND)
  -> connect modules from above
  8x 5V/GND (Sourced from LM2596)
  2x I2C_CLK/I2C_DAT (Sourced from ESP32 for OLED + IMU)
  4x 3.3V/GND (Sourced from ESP32 3.3V Out)
  :: Color-Coding Voltage::
  BLUE: 7.4V - 8.4V (from LiPo 2S)
  CYAN: 6,5V (from XL4016/SZBK07)
  VIOLETT: 5V (from LM2596)
  RED: 3.3V (from ESP32's AMS1117)
  :: LiPo 2S ::
  7.4V - 8.4V
  e.g 5000mAh

custom parts:
  ESP32-38PinWide: Generic 38-Pin ESP32 with wide format (only access to one side of pins on a breadboard) based on Stephen Lilley's HiLetgo ESP-WROOM-32 ESP32 ESP-32S Development Board.
  KY-019 5V Relay Module: KY-019 5V Relay module, used to control AC circuits.
  ESP32 - CAM: The ESP32-CAM has a very competitive small-size camera module that can operate independently as a minimum system with a footprint of only 27*40.5*4.5mm and a deep sleep current of up to 6mA.
  12 NeoPixel Ring: 12 ultra bright smart LED NeoPixels are arranged in a circle with 1.5" (37mm) outer diameter. The rings are 'chainable' - connect the output pin of one to the input pin of another. Use only one microcontroller pin to control as many as you can chain together! Each LED is addressable as the driver chip is inside the LED. Each one has ~18mA constant current drive so the color will be very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
  Adafruit PCA9685 PWM/Servo Breakout: Using only two pins, control 16 free-running PWM outputs! I2C-controlled PWM driver with a built in clock. Unlike the TLC5940 family, you do not need to continuously send it signal tying up your microcontroller, its completely free running! 5V compliant, which means you can control it from a 3.3V microcontroller and still safely drive up to 6V outputs (this is good for when you want to control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
  FTDI Basic Programmer: Description: This is the newest revision of our FTDI Basic. We now use a SMD 6-pin header on the bottom, which makes it smaller and more compact. Functionality has remained the same. This is a basic breakout board for the FTDI FT232RL USB to serial IC. The pinout of this board matches the FTDI cable to work with official Arduino and cloned 3.3V Arduino boards. It can also be used for general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
  Waterproof Pushbutton (white): Waterproof Illuminated Pushbutton (white)
  ACS712 Current Sensor 5A 20A 30A: Remix by Michael Kubina http://www.kubina.info Original by: https://forum.fritzing.org/t/current-sensor-5a-acs712/7694 https://forum.fritzing.org/u/ArtHome ArtHome12@gmail.com
